// Logisim project alu.circ as structural Verilog: 15 circuits, main circuit alu
module alu (
  input  [3:0] a_in,
  input  [3:0] b_in,
  input  [3:0] opcode,
  output [3:0] c_out,
  output [3:0] extra
);

  wire opcode_decoder_1_is_arith, opcode_decoder_1_is_default;
  wire [3:0] arithmetic_unit_1_result, arithmetic_unit_1_subborrow_addcarry_divremainder_muloverflow,
       logic_unit_1_out_4, multiplexer_1_out, undriven;

  logic_unit logic_unit_1 (.a_in(a_in), .b_in(b_in), .opcode(opcode), .out_4(logic_unit_1_out_4));
  Multiplexer #(.width(4)) multiplexer_1 (
    .in0(logic_unit_1_out_4), .in1(arithmetic_unit_1_result), .out(multiplexer_1_out),
    .sel(opcode_decoder_1_is_arith));
  arithmetic_unit arithmetic_unit_1 (
    .a_in(a_in), .b_in(b_in), .opcode(opcode), .result(arithmetic_unit_1_result),
    .subborrow_addcarry_divremainder_muloverflow(arithmetic_unit_1_subborrow_addcarry_divremainder_muloverflow));
  opcode_decoder opcode_decoder_1 (
    .opcode(opcode), .is_arith(opcode_decoder_1_is_arith), .is_default(opcode_decoder_1_is_default));
  // NoConnect on undriven
  Multiplexer #(.width(4)) multiplexer_2 (
    .in0(multiplexer_1_out), .in1(b_in), .out(c_out), .sel(opcode_decoder_1_is_default));
  Multiplexer #(.width(4)) multiplexer_3 (
    .in0(arithmetic_unit_1_subborrow_addcarry_divremainder_muloverflow), .in1(undriven), .out(extra),
    .sel(opcode_decoder_1_is_default));
endmodule

module arithmetic_unit (
  input  [3:0] a_in,
  input  [3:0] b_in,
  input  [3:0] opcode,
  output [3:0] result,
  output [3:0] subborrow_addcarry_divremainder_muloverflow
);

  wire addsub_4_1_carry_out, not_1_out, not_2_out;
  wire [3:0] addsub_4_1_sum, div_4_1_quotient, div_4_1_remainder, mul_4_1_overflow, mul_4_1_product,
       multiplexer_1_out, multiplexer_2_out;

  not not_1 (not_1_out, opcode[1]);
  addsub_4 addsub_4_1 (
    .is_sub(not_1_out), .a_in(a_in), .b_in(b_in), .sum(addsub_4_1_sum), .carry_out(addsub_4_1_carry_out));
  div_4 div_4_1 (.a_in(a_in), .b_in(b_in), .quotient(div_4_1_quotient), .remainder(div_4_1_remainder));
  mul_4 mul_4_1 (.a_in(a_in), .b_in(b_in), .product(mul_4_1_product), .overflow(mul_4_1_overflow));
  Multiplexer #(.width(4)) multiplexer_1 (
    .in0(div_4_1_quotient), .in1(mul_4_1_product), .out(multiplexer_1_out), .sel(opcode[1]));
  Multiplexer #(.width(4)) multiplexer_2 (
    .in0(div_4_1_remainder), .in1(mul_4_1_overflow), .out(multiplexer_2_out), .sel(opcode[1]));
  assign subborrow_addcarry_divremainder_muloverflow[0] = not_2_out ? addsub_4_1_carry_out : 1'bz;  // Controlled_Buffer controlled_buffer_1
  not not_2 (not_2_out, opcode[3]);
  Multiplexer #(.width(4)) multiplexer_3 (.in0(addsub_4_1_sum), .in1(multiplexer_1_out), .out(result), .sel(opcode[3]));
  assign subborrow_addcarry_divremainder_muloverflow = opcode[3] ? multiplexer_2_out : 4'bz;  // Controlled_Buffer controlled_buffer_2
endmodule

module logic_unit (
  input  [3:0] a_in,
  input  [3:0] b_in,
  input  [3:0] opcode,
  output [3:0] out_4
);

  wire [3:0] and_4_1_c, multiplexer_1_out, not_1_out, or_4_1_c, shift_rol_1_result, xor_4_1_c;

  and_4 and_4_1 (.a(a_in), .b(b_in), .c(and_4_1_c));
  or_4 or_4_1 (.a(a_in), .b(b_in), .c(or_4_1_c));
  xor_4 xor_4_1 (.a(a_in), .b(b_in), .c(xor_4_1_c));
  shift_rol shift_rol_1 (.a_in(a_in), .is_rol(opcode[2]), .is_right(opcode[1]), .result(shift_rol_1_result));
  assign not_1_out = ~xor_4_1_c;  // NOT_Gate not_1, 4 bits wide
  Multiplexer #(.select(2), .width(4)) multiplexer_1 (
    .in0(and_4_1_c), .in1(or_4_1_c), .in2(xor_4_1_c), .in3(not_1_out), .out(multiplexer_1_out),
    .sel(opcode[2:1]));
  Multiplexer #(.width(4)) multiplexer_2 (
    .in0(multiplexer_1_out), .in1(shift_rol_1_result), .out(out_4), .sel(opcode[3]));
endmodule

module half_adder (
  input  a_in,
  input  b_in,
  output sum,
  output carry_out
);

  xor xor_1 (sum, a_in, b_in);
  and and_1 (carry_out, a_in, b_in);
endmodule

module full_adder (
  input  carry_in,
  input  a_in,
  input  b_in,
  output sum,
  output carry_out
);

  wire half_adder_1_carry_out, half_adder_1_sum, half_adder_2_carry_out;

  half_adder half_adder_1 (.a_in(a_in), .b_in(b_in), .sum(half_adder_1_sum), .carry_out(half_adder_1_carry_out));
  half_adder half_adder_2 (.a_in(carry_in), .b_in(half_adder_1_sum), .sum(sum), .carry_out(half_adder_2_carry_out));
  xor xor_1 (carry_out, half_adder_2_carry_out, half_adder_1_carry_out);
endmodule

module adder_4 (
  input  [3:0] a_in,
  input  [3:0] b_in,
  output [3:0] sum,
  output carry_out
);

  wire full_adder_1_carry_out, full_adder_2_carry_out, half_adder_1_carry_out;

  half_adder half_adder_1 (.a_in(a_in[0]), .b_in(b_in[0]), .sum(sum[0]), .carry_out(half_adder_1_carry_out));
  full_adder full_adder_1 (
    .carry_in(half_adder_1_carry_out), .a_in(a_in[1]), .b_in(b_in[1]), .sum(sum[1]),
    .carry_out(full_adder_1_carry_out));
  full_adder full_adder_2 (
    .carry_in(full_adder_1_carry_out), .a_in(a_in[2]), .b_in(b_in[2]), .sum(sum[2]),
    .carry_out(full_adder_2_carry_out));
  full_adder full_adder_3 (
    .carry_in(full_adder_2_carry_out), .a_in(a_in[3]), .b_in(b_in[3]), .sum(sum[3]), .carry_out(carry_out));
endmodule

module mul_4 (
  input  [3:0] a_in,
  input  [3:0] b_in,
  output [3:0] product,
  output [3:0] overflow
);

  wire [3:0] and_4_2_c, and_4_3_c, and_4_4_c;
  wire [3:1] adder_4_1_sum, adder_4_2_sum, and_4_1_c;
  wire [3:3] adder_4_1_carry_out, adder_4_2_carry_out;

  and_4 and_4_1 (.a(a_in), .b({4{b_in[0]}}), .c({and_4_1_c, product[0]}));
  and_4 and_4_2 (.a(a_in), .b({4{b_in[1]}}), .c(and_4_2_c));
  and_4 and_4_3 (.a(a_in), .b({4{b_in[2]}}), .c(and_4_3_c));
  and_4 and_4_4 (.a(a_in), .b({4{b_in[3]}}), .c(and_4_4_c));
  adder_4 adder_4_1 (
    .a_in({1'b0, and_4_1_c}), .b_in(and_4_2_c), .sum({adder_4_1_sum, product[1]}),
    .carry_out(adder_4_1_carry_out[3]));
  adder_4 adder_4_2 (
    .a_in({adder_4_1_carry_out[3], adder_4_1_sum}), .b_in(and_4_3_c), .sum({adder_4_2_sum, product[2]}),
    .carry_out(adder_4_2_carry_out[3]));
  adder_4 adder_4_3 (
    .a_in({adder_4_2_carry_out[3], adder_4_2_sum}), .b_in(and_4_4_c), .sum({overflow[2:0], product[3]}),
    .carry_out(overflow[3]));
endmodule

module and_4 (
  input  [3:0] a,
  input  [3:0] b,
  output [3:0] c
);

  and and_1 (c[0], a[0], b[0]);
  and and_2 (c[1], a[1], b[1]);
  and and_3 (c[2], a[2], b[2]);
  and and_4 (c[3], a[3], b[3]);
endmodule

module or_4 (
  input  [3:0] a,
  input  [3:0] b,
  output [3:0] c
);

  or or_1 (c[0], a[0], b[0]);
  or or_2 (c[1], a[1], b[1]);
  or or_3 (c[2], a[2], b[2]);
  or or_4 (c[3], a[3], b[3]);
endmodule

module xor_4 (
  input  [3:0] a,
  input  [3:0] b,
  output [3:0] c
);

  xor xor_1 (c[0], a[0], b[0]);
  xor xor_2 (c[1], a[1], b[1]);
  xor xor_3 (c[2], a[2], b[2]);
  xor xor_4 (c[3], a[3], b[3]);
endmodule

module div_4 (
  input  [3:0] a_in,
  input  [3:0] b_in,
  output [3:0] quotient,
  output [3:0] remainder
);

  wire subtractor_4_1_borrow, subtractor_4_2_borrow, subtractor_4_3_borrow, subtractor_4_4_borrow;
  wire [3:0] subtractor_4_1_diff, subtractor_4_2_diff, subtractor_4_3_diff, subtractor_4_4_diff;
  wire [3:1] multiplexer_1_out, multiplexer_2_out, multiplexer_3_out;
  wire [3:3] multiplexer_1_out_2, multiplexer_2_out_2, multiplexer_3_out_2;

  subtractor_4 subtractor_4_1 (
    .a_in({3'b000, a_in[3]}), .b_in(b_in), .diff(subtractor_4_1_diff), .borrow(subtractor_4_1_borrow));
  not not_1 (quotient[3], subtractor_4_1_borrow);
  subtractor_4 subtractor_4_2 (
    .a_in({multiplexer_1_out, a_in[2]}), .b_in(b_in), .diff(subtractor_4_2_diff),
    .borrow(subtractor_4_2_borrow));
  not not_2 (quotient[2], subtractor_4_2_borrow);
  subtractor_4 subtractor_4_3 (
    .a_in({multiplexer_2_out, a_in[1]}), .b_in(b_in), .diff(subtractor_4_3_diff),
    .borrow(subtractor_4_3_borrow));
  not not_3 (quotient[1], subtractor_4_3_borrow);
  subtractor_4 subtractor_4_4 (
    .a_in({multiplexer_3_out, a_in[0]}), .b_in(b_in), .diff(subtractor_4_4_diff),
    .borrow(subtractor_4_4_borrow));
  not not_4 (quotient[0], subtractor_4_4_borrow);
  Multiplexer #(.width(4)) multiplexer_1 (
    .in0({3'b000, a_in[3]}), .in1(subtractor_4_1_diff), .out({multiplexer_1_out_2[3], multiplexer_1_out}),
    .sel(quotient[3]));
  Multiplexer #(.width(4)) multiplexer_2 (
    .in0({multiplexer_1_out, a_in[2]}), .in1(subtractor_4_2_diff),
    .out({multiplexer_2_out_2[3], multiplexer_2_out}), .sel(quotient[2]));
  Multiplexer #(.width(4)) multiplexer_3 (
    .in0({multiplexer_2_out, a_in[1]}), .in1(subtractor_4_3_diff),
    .out({multiplexer_3_out_2[3], multiplexer_3_out}), .sel(quotient[1]));
  Multiplexer #(.width(4)) multiplexer_4 (
    .in0({multiplexer_3_out, a_in[0]}), .in1(subtractor_4_4_diff), .out(remainder), .sel(quotient[0]));
endmodule

module addsub_4 (
  input  is_sub,
  input  [3:0] a_in,
  input  [3:0] b_in,
  output [3:0] sum,
  output carry_out
);

  wire full_adder_1_carry_out, full_adder_2_carry_out, full_adder_3_carry_out, full_adder_4_carry_out,
       xor_1_out, xor_2_out, xor_3_out, xor_4_out;

  xor xor_1 (xor_1_out, b_in[0], is_sub);
  xor xor_2 (xor_2_out, b_in[1], is_sub);
  xor xor_3 (xor_3_out, b_in[2], is_sub);
  xor xor_4 (xor_4_out, b_in[3], is_sub);
  full_adder full_adder_1 (
    .carry_in(is_sub), .a_in(a_in[0]), .b_in(xor_1_out), .sum(sum[0]), .carry_out(full_adder_1_carry_out));
  full_adder full_adder_2 (
    .carry_in(full_adder_1_carry_out), .a_in(a_in[1]), .b_in(xor_2_out), .sum(sum[1]),
    .carry_out(full_adder_2_carry_out));
  full_adder full_adder_3 (
    .carry_in(full_adder_2_carry_out), .a_in(a_in[2]), .b_in(xor_3_out), .sum(sum[2]),
    .carry_out(full_adder_3_carry_out));
  full_adder full_adder_4 (
    .carry_in(full_adder_3_carry_out), .a_in(a_in[3]), .b_in(xor_4_out), .sum(sum[3]),
    .carry_out(full_adder_4_carry_out));
  xor xor_5 (carry_out, full_adder_4_carry_out, is_sub);
endmodule

module subtractor_4 (
  input  [3:0] a_in,
  input  [3:0] b_in,
  output [3:0] diff,
  output borrow
);

  wire full_adder_1_carry_out, full_adder_2_carry_out, full_adder_3_carry_out, full_adder_4_carry_out,
       not_1_out, not_2_out, not_3_out, not_4_out;

  not not_1 (not_1_out, b_in[0]);
  not not_2 (not_2_out, b_in[1]);
  not not_3 (not_3_out, b_in[2]);
  not not_4 (not_4_out, b_in[3]);
  full_adder full_adder_1 (
    .carry_in(1'b1), .a_in(a_in[0]), .b_in(not_1_out), .sum(diff[0]), .carry_out(full_adder_1_carry_out));
  full_adder full_adder_2 (
    .carry_in(full_adder_1_carry_out), .a_in(a_in[1]), .b_in(not_2_out), .sum(diff[1]),
    .carry_out(full_adder_2_carry_out));
  full_adder full_adder_3 (
    .carry_in(full_adder_2_carry_out), .a_in(a_in[2]), .b_in(not_3_out), .sum(diff[2]),
    .carry_out(full_adder_3_carry_out));
  full_adder full_adder_4 (
    .carry_in(full_adder_3_carry_out), .a_in(a_in[3]), .b_in(not_4_out), .sum(diff[3]),
    .carry_out(full_adder_4_carry_out));
  not not_5 (borrow, full_adder_4_carry_out);
endmodule

module shift_rol (
  input  [3:0] a_in,
  input  is_rol,
  input  is_right,
  output [3:0] result
);

  wire [0:0] and_1_out;
  wire [3:3] and_2_out;

  and and_1 (and_1_out[0], is_rol, a_in[3]);
  and and_2 (and_2_out[3], is_rol, a_in[0]);
  Multiplexer #(.width(4)) multiplexer_1 (
    .in0({a_in[2:0], and_1_out[0]}), .in1({and_2_out[3], a_in[3:1]}), .out(result), .sel(is_right));
endmodule

module opcode_decoder (
  input  [3:0] opcode,
  output is_arith,
  output is_default
);

  and and_1 (is_default, opcode[0], opcode[2]);
  nor nor_1 (is_arith, opcode[0], opcode[2]);
endmodule
