// Logisim project xx.circ as structural Verilog: 4 circuits, main circuit main
module main (
);

  wire and_1_out, bcd_to_7_segment_decoder_2_p1, bcd_to_7_segment_decoder_6_p1, binary_to_bcd_converter_1_p2,
       binary_to_bcd_converter_2_p2, binary_to_bcd_converter_2_p4, binary_to_bcd_converter_3_p2, clock_1_out,
       clock_2_out, is_first_q, is_first_qn, multiplexer_1_out, multiplexer_2_out, roll_out, rst_out,
       win_lose_1_continue, win_lose_1_is_lose, win_lose_1_is_win, win_lose_2_1_continue,
       win_lose_2_1_is_lose, win_lose_2_1_is_win;
  wire [2:0] adder_1_out, ctr1_current_count, ctr2_current_count;
  wire [3:0] point_q, sum_q;
  wire [3:3] adder_1_cout;

  Button rst (.out(rst_out));
  Button roll (.out(roll_out));
  Clock #(.highDuration(5)) clock_1 (.out(clock_1_out));
  Clock #(.highDuration(2), .lowDuration(3)) clock_2 (.out(clock_2_out));
  counter1to6 ctr1 (.clk(clock_1_out), .rst(rst_out), .current_count(ctr1_current_count));
  counter1to6 ctr2 (.clk(clock_2_out), .rst(rst_out), .current_count(ctr2_current_count));
  Hex_Digit_Display ctr1_value (.value({1'b0, ctr1_current_count}));  // open: dp
  Adder #(.width(3)) adder_1 (
    .a(ctr1_current_count), .b(ctr2_current_count), .out(adder_1_out), .cout(adder_1_cout[3]));  // open: cin
  Hex_Digit_Display ctr2_value (.value({1'b0, ctr2_current_count}));  // open: dp
  _7_Segment_Display u_7_segment_display_1 ();  // open: g, f, a, b, e, d, c, dp
  // BCD_to_7_Segment_decoder bcd_to_7_segment_decoder_1: pin names not known
  Register #(.width(4)) sum (
    .D({adder_1_cout[3], adder_1_out}), .en(and_1_out), .clk(roll_out), .Q(sum_q), .clr(rst_out));
  and and_1 (and_1_out, win_lose_2_1_continue, is_first_qn);
  D_Flip_Flop is_first (.D(1'b0), .clk(roll_out), .Q(is_first_q), .Qn(is_first_qn), .preset(rst_out));  // open: reset
  _7_Segment_Display u_7_segment_display_2 ();  // open: g, f, a, b, e, d, c, dp
  // BCD_to_7_Segment_decoder bcd_to_7_segment_decoder_2: pin names not known; wires that end beside it: bcd_to_7_segment_decoder_2_p1
  // Binary_to_BCD_converter #(.binvalue(4)) binary_to_bcd_converter_1: pin names not known; wires that end beside it: {adder_1_cout[3], adder_1_out}, binary_to_bcd_converter_1_p2, binary_to_bcd_converter_1_p2, bcd_to_7_segment_decoder_2_p1
  _7_Segment_Display u_7_segment_display_3 ();  // open: g, f, a, b, e, d, c, dp
  // BCD_to_7_Segment_decoder bcd_to_7_segment_decoder_3: pin names not known
  // Binary_to_BCD_converter #(.binvalue(4)) binary_to_bcd_converter_2: pin names not known; wires that end beside it: sum_q, binary_to_bcd_converter_2_p2, binary_to_bcd_converter_2_p2, binary_to_bcd_converter_2_p4
  Register #(.width(4)) point (
    .D({adder_1_cout[3], adder_1_out}), .en(is_first_q), .clk(roll_out), .Q(point_q), .clr(rst_out));
  _7_Segment_Display u_7_segment_display_4 ();  // open: g, f, a, b, e, d, c, dp
  // BCD_to_7_Segment_decoder bcd_to_7_segment_decoder_4: pin names not known; wires that end beside it: binary_to_bcd_converter_2_p4
  _7_Segment_Display u_7_segment_display_5 ();  // open: g, f, a, b, e, d, c, dp
  // BCD_to_7_Segment_decoder bcd_to_7_segment_decoder_5: pin names not known
  _7_Segment_Display u_7_segment_display_6 ();  // open: g, f, a, b, e, d, c, dp
  // BCD_to_7_Segment_decoder bcd_to_7_segment_decoder_6: pin names not known; wires that end beside it: bcd_to_7_segment_decoder_6_p1
  // Binary_to_BCD_converter #(.binvalue(4)) binary_to_bcd_converter_3: pin names not known; wires that end beside it: point_q, binary_to_bcd_converter_3_p2, binary_to_bcd_converter_3_p2, bcd_to_7_segment_decoder_6_p1
  win_lose win_lose_1 (
    .sum(point_q), .is_win(win_lose_1_is_win), .\continue (win_lose_1_continue), .is_lose(win_lose_1_is_lose));
  win_lose_2 win_lose_2_1 (
    .sum(sum_q), .point(point_q), .is_first(is_first_q), .is_lose(win_lose_2_1_is_lose),
    .is_win(win_lose_2_1_is_win), .\continue (win_lose_2_1_continue));
  Multiplexer multiplexer_1 (
    .in0(win_lose_1_is_win), .in1(win_lose_2_1_is_win), .out(multiplexer_1_out), .sel(win_lose_1_continue));
  Multiplexer multiplexer_2 (
    .in0(win_lose_1_is_lose), .in1(win_lose_2_1_is_lose), .out(multiplexer_2_out), .sel(win_lose_1_continue));
  LED win (.in(multiplexer_1_out));
  LED lose (.in(multiplexer_2_out));

  // Notes on the sheet:
  //   running_sum
  //   sum
  //   point
endmodule

module counter1to6 (
  input  clk,
  input  rst,
  output [2:0] current_count
);

  wire and_1_out, and_2_out, nor_1_out, not_1_out, not_2_out, not_3_out, or_1_out, or_2_out, or_3_out;

  not not_1 (not_1_out, current_count[1]);
  not not_2 (not_2_out, current_count[1]);
  nor nor_1 (nor_1_out, current_count[0], current_count[2]);
  and and_1 (and_1_out, current_count[0], not_1_out);
  or or_1 (or_1_out, not_2_out, current_count[0]);
  or or_2 (or_2_out, current_count[1], current_count[2]);
  D_Flip_Flop d_ff_1 (.D(not_3_out), .clk(clk), .Q(current_count[0]), .preset(rst));  // open: Qn, reset
  not not_3 (not_3_out, current_count[0]);
  D_Flip_Flop d_ff_2 (.D(or_3_out), .clk(clk), .Q(current_count[1]), .reset(rst));  // open: Qn, preset
  or or_3 (or_3_out, nor_1_out, and_1_out);
  D_Flip_Flop d_ff_3 (.D(and_2_out), .clk(clk), .Q(current_count[2]), .reset(rst));  // open: Qn, preset
  and and_2 (and_2_out, or_1_out, or_2_out);
endmodule

module win_lose (
  input  [3:0] sum,
  output is_win,
  output \continue ,
  output is_lose
);

  wire comparator_1_eq, comparator_2_eq, comparator_3_eq, comparator_4_eq, comparator_5_eq;

  Comparator #(.mode("unsigned"), .width(4)) comparator_1 (.a(sum), .b(4'b0111), .eq(comparator_1_eq));  // open: gt, lt
  Comparator #(.mode("unsigned"), .width(4)) comparator_2 (.a(sum), .b(4'b1011), .eq(comparator_2_eq));  // open: gt, lt
  Comparator #(.mode("unsigned"), .width(4)) comparator_3 (.a(sum), .b(4'b0010), .eq(comparator_3_eq));  // open: gt, lt
  Comparator #(.mode("unsigned"), .width(4)) comparator_4 (.a(sum), .b(4'b0011), .eq(comparator_4_eq));  // open: gt, lt
  Comparator #(.mode("unsigned"), .width(4)) comparator_5 (.a(sum), .b(4'b1100), .eq(comparator_5_eq));  // open: gt, lt
  or or_1 (is_win, comparator_1_eq, comparator_2_eq);
  or or_2 (is_lose, comparator_3_eq, comparator_4_eq, comparator_5_eq);
  nor nor_1 (\continue , is_win, is_lose);
endmodule

module win_lose_2 (
  input  [3:0] sum,
  input  [3:0] point,
  input  is_first,
  output is_lose,
  output is_win,
  output \continue 
);

  wire comparator_1_eq, comparator_2_eq, nor_1_out, not_1_out;

  Comparator #(.mode("unsigned"), .width(4)) comparator_1 (.a(4'b0111), .b(sum), .eq(comparator_1_eq));  // open: gt, lt
  Comparator #(.mode("unsigned"), .width(4)) comparator_2 (.a(sum), .b(point), .eq(comparator_2_eq));  // open: gt, lt
  nor nor_1 (nor_1_out, comparator_2_eq, comparator_1_eq);
  not not_1 (not_1_out, is_first);
  and and_1 (is_lose, comparator_1_eq, not_1_out);
  and and_2 (is_win, comparator_2_eq, not_1_out);
  or or_1 (\continue , nor_1_out, is_first);
endmodule
